# Fritzing sketch Amiacs Arcade (saved by Fritzing 0.9.4)

parts:
  Part1 = 24-Channel 12-bit PWM LED Driver - SPI [part_number=1429]
  Part2 = Arduino Nano (Rev3.0) (ICSP)
  D1 = Rectifier Diode [part_number=1N4001 package="300 mil [THT]"]
  J6 = single row smd female pin header, 2 pins [form="♀ (female)"]
  JST_SM-2 = single row smd male pin header, 2 pins [form="♂ (male)"]
  JST_SM-1 = double row smd male pin header, 2 pins [form="♂ (male)"]
  JST_SM-3 = single row smd female pin header, 2 pins [form="♀ (female)"]
  J7 = double row smd male pin header, 2 pins [form="♂ (male)"]
  J8 = single row smd female pin header, 2 pins [form="♀ (female)"]
  B-1 = Pushbutton [package=THT]
  K12-1 = female pin header, 3 pins [form="♀ (female)"]
  LED2 = LED - 5mm [color="Blue (525nm)" package="5 mm [THT]"]
  Player_1 = USB connector [package=THT]  # not connected
  K11-1 = female pin header, 3 pins [form="♀ (female)"]
  ST-1 = female pin header, 3 pins [form="♀ (female)"]
  SE-1 = female pin header, 3 pins [form="♀ (female)"]
  R1-1 = female pin header, 3 pins [form="♀ (female)"]
  L1-1 = female pin header, 3 pins [form="♀ (female)"]
  R2-1 = female pin header, 3 pins [form="♀ (female)"]
  L2-1 = female pin header, 3 pins [form="♀ (female)"]
  K4-1 = female pin header, 3 pins [form="♀ (female)"]
  K3-1 = female pin header, 3 pins [form="♀ (female)"]
  K2-1 = female pin header, 3 pins [form="♀ (female)"]
  K1-1 = female pin header, 3 pins [form="♀ (female)"]
  A-1 = Pushbutton [package=THT]
  LED3 = LED - 5mm [color="Blue (525nm)" package="5 mm [THT]"]
  L1-1_2 = Pushbutton [package=THT]
  LED4 = LED - 5mm [color="Blue (525nm)" package="5 mm [THT]"]
  R1-1_2 = Pushbutton [package=THT]
  LED5 = LED - 5mm [color="Blue (525nm)" package="5 mm [THT]"]
  Y-1 = Pushbutton [package=THT]
  L2-1_2 = Pushbutton [package=THT]
  X-1 = Pushbutton [package=THT]
  R2-1_2 = Pushbutton [package=THT]
  LED6 = LED - 5mm [color="Blue (525nm)" package="5 mm [THT]"]
  LED7 = LED - 5mm [color="Blue (525nm)" package="5 mm [THT]"]
  LED8 = LED - 5mm [color="Blue (525nm)" package="5 mm [THT]"]
  LED9 = LED - 5mm [color="Blue (525nm)" package="5 mm [THT]"]
  EXIT-1 = Pushbutton [package=THT]
  LED10 = LED - 5mm [color="Yellow (595nm)" package="5 mm [THT]"]
  SELECT-1 = Pushbutton [package=THT]
  START-1 = Pushbutton [package=THT]
  LED11 = LED - 5mm [color="Blue (525nm)" package="5 mm [THT]"]
  LED12 = LED - 5mm [color="Blue (525nm)" package="5 mm [THT]"]
  HOTKEY-1 = Pushbutton [package=THT]
  LED13 = LED - 5mm [color="Yellow (595nm)" package="5 mm [THT]"]
  JOY1 = Adafruit Arcade Joystick  # not connected
  D3 = Rectifier Diode [part_number=1N4001 package="300 mil [THT]"]
  START-2 = Pushbutton [package=THT]
  SELECT-2 = Pushbutton [package=THT]
  EXIT-2 = Pushbutton [package=THT]
  R2-2 = Pushbutton [package=THT]
  X-2 = Pushbutton [package=THT]
  L2-2 = Pushbutton [package=THT]
  Y-2 = Pushbutton [package=THT]
  R1-2 = Pushbutton [package=THT]
  L1-2 = Pushbutton [package=THT]
  A-2 = Pushbutton [package=THT]
  B-2 = Pushbutton [package=THT]
  K1-2 = female pin header, 3 pins [form="♀ (female)"]
  K2-2 = female pin header, 3 pins [form="♀ (female)"]
  K3-2 = female pin header, 3 pins [form="♀ (female)"]
  K4-2 = female pin header, 3 pins [form="♀ (female)"]
  L2-2_2 = female pin header, 3 pins [form="♀ (female)"]
  R2-2_2 = female pin header, 3 pins [form="♀ (female)"]
  L1-2_2 = female pin header, 3 pins [form="♀ (female)"]
  R1-2_2 = female pin header, 3 pins [form="♀ (female)"]
  SE-2 = female pin header, 3 pins [form="♀ (female)"]
  ST-2 = female pin header, 3 pins [form="♀ (female)"]
  K11-2 = female pin header, 3 pins [form="♀ (female)"]
  K12-2 = female pin header, 3 pins [form="♀ (female)"]
  LED14 = LED - 5mm [color="Red (660nm)" package="5 mm [THT]"]
  LED15 = LED - 5mm [color="Red (660nm)" package="5 mm [THT]"]
  LED16 = LED - 5mm [color="Yellow (595nm)" package="5 mm [THT]"]
  LED17 = LED - 5mm [color="Red (660nm)" package="5 mm [THT]"]
  LED18 = LED - 5mm [color="Red (660nm)" package="5 mm [THT]"]
  LED19 = LED - 5mm [color="Red (660nm)" package="5 mm [THT]"]
  LED20 = LED - 5mm [color="Red (660nm)" package="5 mm [THT]"]
  LED21 = LED - 5mm [color="Red (660nm)" package="5 mm [THT]"]
  LED22 = LED - 5mm [color="Red (660nm)" package="5 mm [THT]"]
  LED23 = LED - 5mm [color="Red (660nm)" package="5 mm [THT]"]
  LED24 = LED - 5mm [color="Red (660nm)" package="5 mm [THT]"]
  Player_2 = USB connector [package=THT]  # not connected
  JOY2 = Adafruit Arcade Joystick  # not connected
  HOTKEY-2 = Pushbutton [package=THT]
  LED25 = LED - 5mm [color="Yellow (595nm)" package="5 mm [THT]"]
  J13 = shrouded pin header, 28 pins [form="♂ (shrouded male)"]
  OPTI-WIZ = USB connector [package=THT]  # not connected
  TRACKBALL = female pin header, 6 pins [form="♀ (female)"]
  LED26 = RGB LED (com. cathode, rgb) [package="5 mm [THT]"]
  J14 = single row smd female pin header, 4 pins [form="♀ (female)"]
  JST_SM-6 = double row smd male pin header, 4 pins [form="♂ (male)"]
  Raspberry_Pi_1 = Raspberry Pi 3 [part_number=RPI-3-V1.2]
  EXTERNAL = USB connector [package=THT]  # not connected
  LiFePO4wered/Pi+_14500 = Lithium Ion Cylindrical Battery 3.7v 2200mAh
  J12 = single row smd male pin header, 2 pins [form="♂ (male)"]
  JST_SM-5 = double row smd female pin header, 2 pins [form="♀ (female)"]
  JST_SM-4 = double row smd female pin header, 4 pins [form="♀ (female)"]
  J10 = single row smd male pin header, 4 pins [form="♂ (male)"]
  D5 = Rectifier Diode [part_number=1N4001 package="300 mil [THT]"]
  J15 = single row smd male pin header, 4 pins [form="♂ (male)"]
  JST_SM-7 = double row smd female pin header, 4 pins [form="♀ (female)"]
  JACK1 = 2.1mm DC Barrel Jack
  J16 = single row smd male pin header, 2 pins [form="♂ (male)"]
  JST_SM-8 = double row smd female pin header, 2 pins [form="♀ (female)"]
  VIN = double row smd female pin header, 2 pins [form="♀ (female)"]

nets:
  N1: Part1.LAT, JST_SM-4.pin1
  N2: Part1.OE, JST_SM-4.pin2
  N3: Part1.CLK, JST_SM-4.pin3
  N4: Part1.DIN, JST_SM-4.pin4
  N5: Part1.GND, J7.pin2, JST_SM-5.pin1
  N6: Part1.+24V, J7.pin1
  N7: Part1.PWM0, LED2.anode
  N8: Part1.PWM1, LED3.anode
  N9: Part1.PWM2, LED6.anode
  N10: Part1.PWM3, LED9.anode
  N11: Part1.PWM4, LED8.anode
  N12: Part1.PWM5, LED7.anode
  N13: Part1.PWM6, LED4.anode
  N14: Part1.PWM7, LED5.anode
  N15: Part1.PWM8, LED12.anode
  N16: Part1.PWM9, LED11.anode
  N17: Part1.PWM10, LED10.anode
  N18: Part1.PWM11, LED13.anode
  N19: Part1.PWM12, LED24.anode
  N20: Part1.PWM13, LED23.anode
  N21: Part1.PWM14, LED20.anode
  N22: Part1.PWM15, LED17.anode
  N23: Part1.PWM16, LED18.anode
  N24: Part1.PWM17, LED19.anode
  N25: Part1.PWM18, LED22.anode
  N26: Part1.PWM19, LED21.anode
  N27: Part1.PWM20, LED14.anode
  N28: Part1.PWM21, LED15.anode
  N29: Part1.PWM22, LED16.anode
  N30: Part1.PWM23, LED25.anode
  N31: Part2.D3, J14.pin2
  N32: Part2.D4, Part2.D5, J14.pin3
  N33: Part2.D6, J14.pin4
  N34: Part2.D7, Part2.D8, J10.pin3
  N35: Part2.D9, Part2.D10, J10.pin4
  N36: Part2.D11/MOSI, Part2.D12/MISO, J10.pin1
  N37: Part2.GND, Part2.RESET, J12.pin2, J15.pin1
  N38: Part2.5V, J14.pin1, J15.pin2
  N39: Part2.A5, J15.pin3
  N40: Part2.A4, J15.pin4
  N41: Part2.AREF, Part2.3V3, Part2.D13/SCK, J10.pin2
  N42: D1.cathode, JST_SM-3.pin2, D3.cathode
  N43: D1.anode, J6.pin2, JST_SM-1.pin1, EXIT-2.leg0, K11-2.pin1, LED16.cathode
  N44: J6.pin1, JST_SM-2.pin2, JST_SM-1.pin2, JST_SM-3.pin1, K11-2.pin3
  N45: JST_SM-2.pin1, D3.anode
  N46: J8.pin1, K11-1.pin3
  N47: J8.pin2, K11-1.pin1, EXIT-1.leg0, LED10.cathode
  N48: B-1.leg0, LED2.cathode, K1-1.pin1
  N49: B-1.leg1, K1-1.pin2
  N50: K12-1.pin1, HOTKEY-1.leg0, LED13.cathode
  N51: K12-1.pin2, HOTKEY-1.leg1
  N52: K11-1.pin2, EXIT-1.leg1
  N53: ST-1.pin1, START-1.leg0, LED11.cathode
  N54: ST-1.pin2, START-1.leg1
  N55: SE-1.pin1, SELECT-1.leg0, LED12.cathode
  N56: SE-1.pin2, SELECT-1.leg1
  N57: R1-1.pin1, R1-1_2.leg0, LED5.cathode
  N58: R1-1.pin2, R1-1_2.leg1
  N59: L1-1.pin1, L1-1_2.leg0, LED4.cathode
  N60: L1-1.pin2, L1-1.pin3, L1-1_2.leg1
  N61: R2-1.pin1, R2-1_2.leg0, LED7.cathode
  N62: R2-1.pin2, R2-1_2.leg1
  N63: L2-1.pin1, L2-1_2.leg0, LED8.cathode
  N64: L2-1.pin2, L2-1_2.leg1
  N65: K4-1.pin1, X-1.leg0, LED9.cathode
  N66: K4-1.pin2, X-1.leg1
  N67: K3-1.pin1, Y-1.leg0, LED6.cathode
  N68: K3-1.pin2, Y-1.leg1
  N69: K2-1.pin1, A-1.leg0, LED3.cathode
  N70: K2-1.pin2, A-1.leg1
  N71: START-2.leg0, ST-2.pin1, LED15.cathode
  N72: START-2.leg1, ST-2.pin2
  N73: SELECT-2.leg0, SE-2.pin1, LED14.cathode
  N74: SELECT-2.leg1, SE-2.pin2
  N75: EXIT-2.leg1, K11-2.pin2
  N76: R2-2.leg0, R2-2_2.pin1, LED19.cathode
  N77: R2-2.leg1, R2-2_2.pin2
  N78: X-2.leg0, K4-2.pin1, LED17.cathode
  N79: X-2.leg1, K4-2.pin2
  N80: L2-2.leg0, L2-2_2.pin1, LED18.cathode
  N81: L2-2.leg1, L2-2_2.pin2
  N82: Y-2.leg0, K3-2.pin1, LED20.cathode
  N83: Y-2.leg1, K3-2.pin2
  N84: R1-2.leg0, R1-2_2.pin1, LED21.cathode
  N85: R1-2.leg1, R1-2_2.pin2
  N86: L1-2.leg0, L1-2_2.pin1, LED22.cathode
  N87: L1-2.leg1, L1-2_2.pin2
  N88: A-2.leg0, K2-2.pin1, LED23.cathode
  N89: A-2.leg1, K2-2.pin2
  N90: B-2.leg0, K1-2.pin1, LED24.cathode
  N91: B-2.leg1, K1-2.pin2
  N92: K12-2.pin1, HOTKEY-2.leg0, LED25.cathode
  N93: K12-2.pin2, HOTKEY-2.leg1
  N94: J13.pin3, J13.pin4, TRACKBALL.pin2
  N95: J13.pin12, J13.pin13, TRACKBALL.pin3
  N96: J13.pin14, TRACKBALL.pin6
  N97: J13.pin15, TRACKBALL.pin5
  N98: J13.pin16, J13.pin17, TRACKBALL.pin4
  N99: J13.pin25, J13.pin26, TRACKBALL.pin1
  N100: LED26.red_anode, JST_SM-6.pin3
  N101: LED26.common_cathode, JST_SM-6.pin4
  N102: LED26.green_anode, JST_SM-6.pin2
  N103: LED26.blue_anode, JST_SM-6.pin1
  N104: Raspberry_Pi_1.GPIO2, JST_SM-7.pin1
  N105: Raspberry_Pi_1.GPIO3, JST_SM-7.pin2
  N106: LiFePO4wered/Pi+_14500.positive, D5.anode
  N107: LiFePO4wered/Pi+_14500.negative, JST_SM-7.pin4
  N108: D5.cathode, JST_SM-7.pin3
  N109: JACK1.center, JST_SM-8.pin1
  N110: JACK1.sleeve, JST_SM-8.pin2
  N111: J16.pin1, VIN.pin2
  N112: J16.pin2, VIN.pin1

notes:
  The V+ (black) and GND (red) wire colors coming from the controllers are opposite. This connection will look wrong.
  These diodes are used to keep the voltage from going from one controller to the other.
  Most components are representations. The properties do not reflect the actual part.
  The pushbuttons and LEDs represent the arcade buttons.
  The TLC5947 is upside down in the physical panel. So the pins are mirrored from shown.
  The Raspberry Pi is upside down in the physical panel. So the connections are mirrored from shown.
  Connected to VOUT on LiFePO4wered.
  Without this diode, removing power from LiFePO4wered rebooted the Pi without running the shutdown script.
  This power source might not be the best solution. Could try getting power from the Pi's GPIO pins.
  This layout of components represents what is seen when the control panel is bottom up. As in how it would be oriented to access the components.
  SPI
  I2C
  I2C SDA
  I2C SCL
  SPI CLK
  SPI OE
  SPI LAT
  SPI DIN
  Connected to VIN on
  LiFePO4wered.

custom parts:
  24-Channel 12-bit PWM LED Driver - SPI: This breakout board for the TLC5947 PWM driver chip can control 24 separate channels of 12-bit PWM output. Designed (and ideal) for LED control, this board is NOT good for driving servos. Only three "SPI" pins are required to send data (our Arduino library shows how to to use any digital microcontroller pins). Best of all, the design is completely chainable. As long as there's enough power for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
  Lithium Ion Cylindrical Battery 3.7v 2200mAh: This lithium ion battery has a capacity of 2200mAh and a protection circuit that provides over-voltage, under-voltage and over-current protection. This cell can provide 2C of peak current (4400mA). Note that these batteries are not designed to sustain such high loads, we suggest keeping any constant current draw under about 0.5C (1 Amp).
  2.1mm DC Barrel Jack: 2.1mm DC Barrel Jack with Thru-Hole Connectors (breadboardable)
