# Fritzing sketch Test Amiacs Light Controller (saved by Fritzing 1.0.2b)
breadboards: 4

parts:
  Ambient_RGB_LED_Strip = RGB Strip LED
  Part1 = Arduino Nano (Rev3.0)
  R1 = Resistor [tolerance=±5% resistance=220 power=0.25W package=THT]
  R2 = Resistor [tolerance=±5% resistance=220 power=0.25W package=THT]
  R3 = Resistor [tolerance=±5% resistance=220 power=0.25W package=THT]
  Q1 = Basic FET N-Channel [package="TO220 [THT]"]
  HLK-PM1 = HLK-PM12 [part_number=HLK-PM12]
  R4 = Resistor [tolerance=±5% resistance=220 power=0.25W package=THT]
  J2 = Camdenboss CTB0158-4 [part_number=CTB0158-4 package=THT]
  J3 = Camdenboss CTB0158-2 [part_number=CTB0158-2 package=THT]
  J5 = male pin header, 4 pins [form="♂ (male)"]
  J6 = male pin header, 4 pins [form="♂ (male)"]  # not connected
  Marquee_White_LED_Strip = LED - 5mm [color="White (6500K)" current=0.030A package="5 mm [THT]"]
  LED21 = LED - 3mm [color="Blue (525nm)" current=0.030A package="3 mm [THT]"]
  LED22 = LED - 3mm [color="Blue (525nm)" current=0.030A package="3 mm [THT]"]
  LED23 = LED - 3mm [color="Blue (525nm)" current=0.030A package="3 mm [THT]"]
  LED24 = LED - 3mm [color="Blue (525nm)" current=0.030A package="3 mm [THT]"]
  LED25 = LED - 3mm [color="Blue (525nm)" current=0.030A package="3 mm [THT]"]
  LED26 = LED - 3mm [color="Blue (525nm)" current=0.030A package="3 mm [THT]"]
  LED27 = LED - 3mm [color="Blue (525nm)" current=0.030A package="3 mm [THT]"]
  LED28 = LED - 3mm [color="Blue (525nm)" current=0.030A package="3 mm [THT]"]
  LED29 = LED - 3mm [color="Blue (525nm)" current=0.030A package="3 mm [THT]"]
  LED30 = LED - 3mm [color="Blue (525nm)" current=0.030A package="3 mm [THT]"]
  LED31 = LED - 3mm [color="Red (633nm)" current=0.030A package="3 mm [THT]"]
  LED32 = LED - 3mm [color="Red (633nm)" current=0.030A package="3 mm [THT]"]
  LED33 = LED - 3mm [color="Red (633nm)" current=0.030A package="3 mm [THT]"]
  LED34 = LED - 3mm [color="Red (633nm)" current=0.030A package="3 mm [THT]"]
  LED35 = LED - 3mm [color="Red (633nm)" current=0.030A package="3 mm [THT]"]
  LED36 = LED - 3mm [color="Red (633nm)" current=0.030A package="3 mm [THT]"]
  LED37 = LED - 3mm [color="Red (633nm)" current=0.030A package="3 mm [THT]"]
  LED38 = LED - 3mm [color="Red (633nm)" current=0.030A package="3 mm [THT]"]
  LED39 = LED - 3mm [color="Red (633nm)" current=0.030A package="3 mm [THT]"]
  LED40 = LED - 3mm [color="Red (633nm)" current=0.030A package="3 mm [THT]"]
  LED41 = LED - 3mm [color="Yellow (595nm)" current=0.030A package="3 mm [THT]"]
  LED42 = LED - 3mm [color="Yellow (595nm)" current=0.030A package="3 mm [THT]"]
  LED43 = LED - 3mm [color="Yellow (595nm)" current=0.030A package="3 mm [THT]"]
  LED44 = LED - 3mm [color="Yellow (595nm)" current=0.030A package="3 mm [THT]"]
  Part2 = 24-Channel 12-bit PWM LED Driver - SPI [part_number=1429]
  Trackball = RGB LED (com. cathode, rgb) [color="Red (633nm)" current=0.030A package="5 mm [THT]"]

nets:
  N1: Ambient_RGB_LED_Strip.Common_Connect, J2.terminal_4
  N2: Ambient_RGB_LED_Strip.Green_Connect, J2.terminal_3
  N3: Ambient_RGB_LED_Strip.Red_Connect, J2.terminal_2
  N4: Ambient_RGB_LED_Strip.Blue_Connect, J2.terminal_1
  GND: Part1.GND, J5.pin1, Part2.GND, Trackball.common_cathode
  N5: Part1.D3, R1.Pin_1
  N6: Part1.D5, R2.Pin_1
  N7: Part1.D6, R3.Pin_1
  N8: Part1.D9, R4.Pin_1
  N9: Part1.D10, Part2.LAT
  N10: Part1.D11/MOSI, J5.pin3
  N11: Part1.D12/MISO, Part2.DIN
  N12: Part1.5V, J5.pin2, LED21.anode, LED22.anode, LED23.anode, LED24.anode, LED25.anode, LED26.anode, LED27.anode, LED28.anode, LED29.anode, LED30.anode, LED31.anode, LED32.anode, LED33.anode, LED34.anode, LED35.anode, LED36.anode, LED37.anode, LED38.anode, LED39.anode, LED40.anode, LED41.anode, LED42.anode, LED43.anode, LED44.anode, Part2.+24V
  N13: Part1.D13/SCK, J5.pin4, Part2.CLK
  N14: R1.Pin_0, Trackball.red_anode
  N15: R2.Pin_0, Trackball.green_anode
  N16: R3.Pin_0, Trackball.blue_anode
  N17: Q1.gate, R4.Pin_0
  N18: Q1.drain, Marquee_White_LED_Strip.cathode
  N19: Q1.source, HLK-PM1.-Vo, J3.terminal_2
  N20: HLK-PM1.+Vo, J3.terminal_1, Marquee_White_LED_Strip.anode
  N21: LED21.cathode, Part2.PWM0
  N22: LED22.cathode, Part2.PWM1
  N23: LED23.cathode, Part2.PWM6
  N24: LED24.cathode, Part2.PWM5
  N25: LED25.cathode, Part2.PWM2
  N26: LED26.cathode, Part2.PWM4
  N27: LED27.cathode, Part2.PWM3
  N28: LED28.cathode, Part2.PWM7
  N29: LED29.cathode, Part2.PWM8
  N30: LED30.cathode, Part2.PWM9
  N31: LED31.cathode, Part2.PWM12
  N32: LED32.cathode, Part2.PWM13
  N33: LED33.cathode, Part2.PWM18
  N34: LED34.cathode, Part2.PWM17
  N35: LED35.cathode, Part2.PWM14
  N36: LED36.cathode, Part2.PWM16
  N37: LED37.cathode, Part2.PWM15
  N38: LED38.cathode, Part2.PWM19
  N39: LED39.cathode, Part2.PWM20
  N40: LED40.cathode, Part2.PWM21
  N41: LED41.cathode, Part2.PWM11
  N42: LED42.cathode, Part2.PWM10
  N43: LED43.cathode, Part2.PWM23
  N44: LED44.cathode, Part2.PWM22

notes:
  The actual trackball LEDs have resistors
  built in.
  It also uses a common anode (+5V). This schematic is for a common cathode (ground).
  This group of parts represents an SPI based P9813 LED strip driver board.
  MOSI
  SCK
  CIN
  DIN
  VCC
  GND

custom parts:
  RGB Strip LED: A tri-color Strip LED with red, green and blue. Based on LED SMD 5050 RGB Pin order: common cathode - green - red - blue
  24-Channel 12-bit PWM LED Driver - SPI: This breakout board for the TLC5947 PWM driver chip can control 24 separate channels of 12-bit PWM output. Designed (and ideal) for LED control, this board is NOT good for driving servos. Only three "SPI" pins are required to send data (our Arduino library shows how to to use any digital microcontroller pins). Best of all, the design is completely chainable. As long as there's enough power for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
